// Logisim project RISC 32 BIT ALU.circ as structural Verilog: 1 circuit, main circuit main
module main (
);

  wire A, clock_1_out, L, subtractor_1_bout, xor_2_out;
  wire [31:0] adder_1_out, adder_2_out, and_1_out, divider_1_out, divider_2_rem, multiplexer_1_out,
       multiplexer_2_out, multiplexer_3_out, multiplier_1_out, or_1_out, RESULT, shifter_1_out,
       shifter_2_out, subtractor_1_out, subtractor_2_out, xor_1_out;

  Clock clock_1 (.out(clock_1_out));
  Adder #(.width(32)) adder_1 (.a(32'hf), .b(32'h4), .out(adder_1_out));  // open: cin, cout
  Subtractor #(.width(32)) subtractor_1 (
    .a(32'hf), .b(32'h4), .out(subtractor_1_out), .bin(1'b0), .bout(subtractor_1_bout));
  Multiplier #(.width(32)) multiplier_1 (.a(32'hf), .b(32'h4), .out(multiplier_1_out));  // open: cin, cout
  Divider #(.width(32)) divider_1 (.a(32'hf), .out(divider_1_out));  // open: b, upper, rem
  Divider #(.width(32)) divider_2 (.a(32'hf), .b(32'h4), .rem(divider_2_rem));  // open: out, upper
  Adder #(.width(32)) adder_2 (.a(32'hf), .b(32'h1), .out(adder_2_out));  // open: cin, cout
  Subtractor #(.width(32)) subtractor_2 (.a(32'hf), .b(32'h1), .out(subtractor_2_out));  // open: bin, bout
  assign and_1_out = 32'hf & 32'h4;  // AND_Gate and_1, 32 bits wide
  assign or_1_out = 32'hf | 32'h4;  // OR_Gate or_1, 32 bits wide
  assign xor_1_out = 32'hf ^ 32'h4;  // XOR_Gate xor_1, 32 bits wide
  Shifter #(.width(32)) shifter_1 (.in(32'hf), .\dist (5'b00100), .out(shifter_1_out));
  Shifter #(.width(32), .shift("lr")) shifter_2 (.in(32'hf), .\dist (5'b00100), .out(shifter_2_out));
  Multiplexer #(.select(3), .width(32)) multiplexer_1 (
    .in0(adder_1_out), .in1(subtractor_1_out), .in2(multiplier_1_out), .in3(divider_1_out),
    .in4(divider_2_rem), .in5(adder_2_out), .in6(subtractor_2_out), .out(multiplexer_1_out), .sel(3'b100),
    .en(1'b1));  // open: in7
  Multiplexer #(.select(3), .width(32)) multiplexer_2 (
    .in0(and_1_out), .in1(or_1_out), .in2(xor_1_out), .in4(shifter_1_out), .in5(shifter_2_out),
    .out(multiplexer_2_out), .sel(3'b100), .en(1'b1));  // open: in3, in6, in7
  // Probe on multiplexer_1_out
  // Probe on multiplexer_2_out
  xor xor_2 (xor_2_out, L, A);
  // Probe on RESULT
  Multiplexer #(.width(32)) multiplexer_3 (
    .in0(multiplexer_1_out), .in1(multiplexer_2_out), .out(multiplexer_3_out), .sel(xor_2_out), .en(1'b1));
  Register #(.width(32)) register_1 (
    .D(multiplexer_3_out), .en(xor_2_out), .Q(RESULT), .clk(clock_1_out));  // open: clr
  and and_2 (L, ~1'b0, ~1'b0, ~1'b1);  // AND_Gate
  and and_3 (A, ~1'b0, ~1'b0, 1'b1);  // AND_Gate
endmodule
