// Logisim project RISC 32 BIT DECODE.circ as structural Verilog: 1 circuit, main circuit main
module main (
  input  [31:0] Instruction,
  input  Clock,
  output out_3,
  output out_4,
  output [2:0] out_5,
  output [2:0] out_6,
  output out_7,
  output out_8,
  output out_9,
  output out_10,
  output out_11,
  output out_12,
  output out_13,
  output out_14,
  output out_15,
  output out_16,
  output out_17,
  output out_18,
  output out_19,
  output out_20,
  output out_21,
  output out_22,
  output out_23,
  output out_24,
  output out_25,
  output out_26,
  output Arithmetic,
  output Logic,
  output BranchJump,
  output RegInstr,
  output Stack,
  output out_32,
  output out_33,
  output out_34,
  output out_35,
  output out_36,
  output out_37,
  output out_38,
  output [7:0] out_39,
  output [7:0] out_40,
  output [7:0] out_41,
  output [1:0] out_42
);

  and and_1 (Arithmetic, ~out_5[2], ~out_5[1], out_5[0]);  // AND_Gate
  and and_2 (Logic, ~out_5[2], ~out_5[1], ~out_5[0]);  // AND_Gate
  and and_3 (BranchJump, ~out_5[2], out_5[1]);  // AND_Gate
  Register #(.width(32)) Instruction_Register (
    .D(Instruction), .en(1'b1), .Q({out_5, out_6, out_42, out_39, out_40, out_41}), .clk(Clock), .clr(1'b0));
  and and_4 (RegInstr, out_5[2], out_5[1], ~out_5[0]);  // AND_Gate
  and and_5 (Stack, out_5[2], ~out_5[1], ~out_5[0]);  // AND_Gate
  Decoder #(.select(3)) decoder_1 (
    .out1(out_12), .out2(out_13), .out3(out_14), .out4(out_15), .out5(out_16), .out6(out_17), .sel(out_6),
    .en(Logic));  // open: out0, out7
  Decoder decoder_2 (.out0(out_18), .out1(out_19), .sel(out_6[0]), .en(Stack));
  Decoder #(.select(3)) decoder_3 (
    .out0(out_20), .out1(out_21), .out2(out_22), .out3(out_23), .out4(out_24), .out5(out_25), .out6(out_26),
    .out7(out_32), .sel(out_6), .en(BranchJump));
  Decoder #(.select(3)) decoder_4 (
    .out0(out_34), .out1(out_35), .out2(out_36), .out3(out_37), .sel(out_6), .en(RegInstr));  // open: out4, out5, out6, out7
  Decoder #(.select(3)) decoder_5 (
    .out0(out_3), .out1(out_4), .out2(out_7), .out3(out_8), .out4(out_9), .out5(out_10), .out6(out_11),
    .sel(out_6), .en(Arithmetic));  // open: out7
  and and_6 (out_38, out_5[0], out_5[1], out_5[2], out_6[0], out_6[1], out_6[2]);
  and and_7 (out_33, BranchJump, out_5[0], ~out_6[0], ~out_6[1], ~out_6[2]);  // AND_Gate

  // Other names for the same wires on the sheet: First[7:0] = out_41; OP2[7:0] = out_41; OP1[7:0] = out_40;
  //   Second[7:0] = out_40; Dest[7:0] = out_39; Third[7:0] = out_39; Fourth[7:0] = {out_5, out_6, out_42};
  //   Number[1:0] = out_42; Instruction_t[2:0] = out_6; IR29 = out_5[0]; Type[2:0] = out_5; IR30 = out_5[1];
  //   IR31 = out_5[2]; ADD = out_3; AND = out_12; BEQ = out_22; BGE = out_24; BGT = out_23; BLEQ = out_25;
  //   BLSS = out_21; BNEQ = out_26; CLR = out_37; CMP = out_15; DEC = out_11; DIV = out_8; HALT = out_38;
  //   INC = out_10; JSR = out_32; JUMP = out_20; LD = out_34; LSH = out_16; MOD = out_9; MOV = out_36; MUL = out_7;
  //   OR = out_13; POP = out_18; PUSH = out_19; RSH = out_17; RTS = out_33; ST = out_35; SUB = out_4; XOR = out_14
endmodule
