// Logisim project RISC 32 BIT MAIN.circ as structural Verilog: 1 circuit, main circuit main
module main (
  input  [31:0] in_1
);

  wire and_3_out, Arithmetic, Clock, clock_1_out, CLR, controlled_buffer_1_out, EnOP1, EnOP2, EnRC, HALT, LD,
       Logic, MOV, multiplexer_2_out, OneAddress, or_1_out, or_2_out, or_3_out, or_4_out, or_6_out, or_7_out,
       ThreeAddress, TwoAddress, ZeroAddress;
  wire [1:0] Num, SelectInput, SelectREG;
  wire [2:0] Instr, OPCODE;
  wire [4:0] REG1, REG2;
  wire [7:0] Dest;
  wire [15:0] Input;
  wire [31:0] multiplexer_1_out, OP1, OP2, Result;

  Clock clock_1 (.out(clock_1_out));
  and and_1 (Clock, clock_1_out, ~HALT);  // AND_Gate
  RISC_32_BIT_ALU_main main_1 (
    .Clock(Clock), .Result(Result), .OP1(OP1), .OP2(OP2), .OpeartionCode(OPCODE), .in_1(Instr));
  RISC_32_BIT_DECODE_main main_2 (
    .Clock(Clock), .out_34(LD), .out_36(MOV), .out_37(CLR), .out_38(HALT), .out_39(Dest),
    .out_40(Input[15:8]), .out_41(Input[7:0]), .out_42(Num), .Instruction(in_1), .Arithmetic(Arithmetic),
    .Logic(Logic), .out_5(Instr), .out_6(OPCODE));  // open: out_3, out_4, out_7, out_8, out_9, out_10, out_11, out_12, out_13, out_14, out_15, out_16, out_17, out_18, out_19, out_20, out_21, out_22, out_23, out_24, out_25, out_26, out_32, out_33, out_35, BranchJump, RegInstr, Stack
  // Probe on Result
  RISC_32_BIT_MEMORY_main main_3 (.in_3(Clock));  // open: in_1, in_2, in_4, in_5, in_6, out_7, out_8
  or or_1 (or_1_out, EnOP1, EnOP2);
  Multiplexer #(.select(2), .width(32)) multiplexer_1 (
    .in0(Result), .in1(OP1), .in2({{16{1'b0}}, Input}), .out(multiplexer_1_out), .sel(SelectInput), .en(1'b1));  // open: in3
  Multiplexer multiplexer_2 (.in0(1'b0), .in1(1'b1), .out(multiplexer_2_out), .sel(CLR), .en(1'b1));
  assign controlled_buffer_1_out = or_1_out ? EnRC : 1'bz;  // Controlled_Buffer controlled_buffer_1
  Pull_Resistor pull_resistor_1 (.node(controlled_buffer_1_out));
  // RISC_32_BIT_REGISTERS_main main_4: pin names not known; wires that end beside it: multiplexer_1_out, Dest[4:0], REG1, REG2, controlled_buffer_1_out, multiplexer_2_out, EnOP1, EnOP2, Clock, OP1, OP2
  Multiplexer #(.select(2), .width(5)) multiplexer_3 (
    .in1(Dest[4:0]), .in2(Dest[4:0]), .in3(Input[12:8]), .out(REG1), .sel(SelectREG), .en(1'b1));  // open: in0
  Multiplexer #(.select(2), .width(5)) multiplexer_4 (
    .in0({5{1'b0}}), .in1({5{1'b0}}), .in2(Input[12:8]), .in3(Input[4:0]), .out(REG2), .sel(SelectREG),
    .en(1'b1));
  or or_2 (or_2_out, ThreeAddress, TwoAddress, OneAddress);
  or or_3 (or_3_out, ThreeAddress, TwoAddress);
  or or_4 (or_4_out, or_2_out, MOV);
  and and_2 (EnOP2, or_3_out, ~ZeroAddress, ~MOV, ~LD);  // AND_Gate
  or or_5 (EnRC, Arithmetic, Logic, MOV, LD);
  and and_3 (and_3_out, TwoAddress, ~MOV);  // AND_Gate
  and and_4 (EnOP1, or_4_out, ~ZeroAddress, ~LD, ~CLR);  // AND_Gate
  Priority_Encoder #(.select(2)) priority_encoder_1 (
    .in1(OneAddress), .in2(and_3_out), .in3(or_6_out), .out(SelectREG));  // open: in0, gs, en_out, en_in
  or or_6 (or_6_out, ThreeAddress, MOV);
  or or_7 (or_7_out, Arithmetic, Logic);
  Priority_Encoder #(.select(2)) priority_encoder_2 (
    .in0(or_7_out), .in1(MOV), .in2(LD), .out(SelectInput));  // open: in3, gs, en_out, en_in
  and and_5 (ThreeAddress, Num[0], Num[1]);
  and and_6 (TwoAddress, ~Num[0], Num[1]);  // AND_Gate
  and and_7 (OneAddress, Num[0], ~Num[1]);  // AND_Gate
  and and_8 (ZeroAddress, ~Num[0], ~Num[1]);  // AND_Gate

  // Other names for the same wires on the sheet: RC[4:0] = Dest[4:0]; O2[7:0] = Input[7:0]; O1[7:0] = Input[15:8]
endmodule
